// Logisim project 2_1 Shift.circ as structural Verilog: 1 circuit, main circuit main
module main (
  input  A_3,
  input  A_2,
  input  A_1,
  input  A_0,
  input  [1:0] ShiftAmountIn,
  input  in_6,
  input  in_7,
  output out_8,
  output out_9,
  output out_10,
  output out_11
);

  wire multiplexer_1_out, multiplexer_2_out, multiplexer_3_out, multiplexer_5_out, multiplexer_7_out,
       multiplexer_9_out, multiplexer_10_out, multiplexer_11_out, multiplexer_13_out, multiplexer_14_out,
       multiplexer_15_out;

  Multiplexer #(.select(2)) multiplexer_1 (
    .in0(A_3), .in1(A_2), .in2(A_1), .in3(A_0), .out(multiplexer_1_out), .sel(ShiftAmountIn));  // open: en
  Multiplexer #(.select(2)) multiplexer_2 (
    .in0(A_3), .out(multiplexer_2_out), .sel(ShiftAmountIn));  // open: in1, in2, in3, en
  Multiplexer #(.select(2)) multiplexer_3 (
    .in0(A_3), .in1(A_3), .in2(A_3), .in3(A_3), .out(multiplexer_3_out), .sel(ShiftAmountIn));  // open: en
  Multiplexer #(.select(2)) multiplexer_4 (
    .in0(multiplexer_13_out), .in1(multiplexer_13_out), .in2(multiplexer_14_out), .in3(multiplexer_15_out),
    .out(out_8), .sel({in_7, in_6}));  // open: en
  Multiplexer #(.select(2)) multiplexer_5 (
    .in0(A_2), .in1(A_1), .in2(A_0), .out(multiplexer_5_out), .sel(ShiftAmountIn));  // open: in3, en
  Multiplexer #(.select(2)) multiplexer_6 (
    .in0(A_2), .in1(A_3), .out(multiplexer_1_out), .sel(ShiftAmountIn));  // open: in2, in3, en
  Multiplexer #(.select(2)) multiplexer_7 (
    .in0(A_2), .in1(A_3), .in2(A_3), .in3(A_3), .out(multiplexer_7_out), .sel(ShiftAmountIn));  // open: en
  Multiplexer #(.select(2)) multiplexer_8 (
    .in0(multiplexer_9_out), .in1(multiplexer_9_out), .in2(multiplexer_10_out), .in3(multiplexer_11_out),
    .out(out_9), .sel({in_7, in_6}));  // open: en
  Multiplexer #(.select(2)) multiplexer_9 (
    .in0(A_1), .in1(A_0), .out(multiplexer_9_out), .sel(ShiftAmountIn));  // open: in2, in3, en
  Multiplexer #(.select(2)) multiplexer_10 (
    .in0(A_1), .in1(A_2), .in2(A_3), .out(multiplexer_10_out), .sel(ShiftAmountIn));  // open: in3, en
  Multiplexer #(.select(2)) multiplexer_11 (
    .in0(A_1), .in1(A_2), .in2(A_3), .in3(A_3), .out(multiplexer_11_out), .sel(ShiftAmountIn));  // open: en
  Multiplexer #(.select(2)) multiplexer_12 (
    .in0(multiplexer_5_out), .in1(multiplexer_5_out), .in2(multiplexer_1_out), .in3(multiplexer_7_out),
    .out(out_10), .sel({in_7, in_6}));  // open: en
  Multiplexer #(.select(2)) multiplexer_13 (
    .in0(A_0), .out(multiplexer_13_out), .sel(ShiftAmountIn));  // open: in1, in2, in3, en
  Multiplexer #(.select(2)) multiplexer_14 (
    .in0(A_0), .in1(A_1), .in2(A_2), .in3(A_3), .out(multiplexer_14_out), .sel(ShiftAmountIn));  // open: en
  Multiplexer #(.select(2)) multiplexer_15 (
    .in0(A_0), .in1(A_1), .in2(A_2), .in3(A_3), .out(multiplexer_15_out), .sel(ShiftAmountIn));  // open: en
  Multiplexer #(.select(2)) multiplexer_16 (
    .in0(multiplexer_1_out), .in1(multiplexer_1_out), .in2(multiplexer_2_out), .in3(multiplexer_3_out),
    .out(out_11), .sel({in_7, in_6}));  // open: en
endmodule
