// Logisim project 2_2 Counter.circ as structural Verilog: 1 circuit, main circuit main
module main (
  input  CountDownIn,
  input  CountUpIn,
  input  in_3,
  input  clkin,
  input  in_5,
  input  EnableIn,
  output out_7,
  output [2:0] Count
);

  wire and_1_out, and_2_out, and_4_out, and_5_out, j_k_ff_1_qn, j_k_ff_2_qn, j_k_ff_3_qn, not_1_out,
       not_2_out, not_3_out, not_4_out, not_5_out, not_6_out, or_1_out, xor_1_out;

  and and_1 (and_1_out, clkin, not_6_out, not_2_out, EnableIn);
  and and_2 (and_2_out, CountUpIn, Count[0], Count[1]);
  or or_1 (or_1_out, and_2_out, out_7);
  J_K_Flip_Flop j_k_ff_1 (
    .J(or_1_out), .K(or_1_out), .clk(and_1_out), .Q(Count[2]), .Qn(j_k_ff_1_qn), .preset(in_3), .reset(in_5));
  and and_3 (out_7, CountDownIn, j_k_ff_2_qn, j_k_ff_3_qn);
  xor xor_1 (xor_1_out, CountUpIn, Count[0]);
  not not_1 (not_1_out, xor_1_out);
  J_K_Flip_Flop j_k_ff_2 (
    .J(not_1_out), .K(not_1_out), .clk(and_1_out), .Q(Count[1]), .Qn(j_k_ff_2_qn), .preset(in_3), .reset(in_5));
  J_K_Flip_Flop j_k_ff_3 (
    .J(1'b1), .K(1'b1), .clk(and_1_out), .Q(Count[0]), .Qn(j_k_ff_3_qn), .preset(in_3), .reset(in_5));
  and and_4 (and_4_out, Count[2], CountUpIn, Count[1], Count[0]);
  not not_2 (not_2_out, and_4_out);
  not not_3 (not_3_out, Count[0]);
  not not_4 (not_4_out, Count[1]);
  not not_5 (not_5_out, Count[2]);
  and and_5 (and_5_out, CountDownIn, not_3_out, not_4_out, not_5_out);
  not not_6 (not_6_out, and_5_out);
endmodule
