// Logisim project 2_3 ALU.circ as structural Verilog
module Carry_Look_Ahead (
  input  A,
  input  B,
  input  Cin,
  output Sum,
  output P,
  output G
);

  wire xor_1_out;

  xor xor_1 (xor_1_out, A, B);
  xor xor_2 (Sum, Cin, xor_1_out);
  or or_1 (P, A, B);
  and and_1 (G, A, B);
endmodule

module Carry_1 (
  input  G_0,
  input  C_0,
  input  P_0,
  output C_1
);

  wire and_1_out;

  and and_1 (and_1_out, C_0, P_0);
  or or_1 (C_1, G_0, and_1_out);
endmodule

module Carry_2 (
  input  G_1,
  input  G_0,
  input  C_0,
  input  P_1,
  input  P_0,
  output C_2
);

  wire and_1_out, and_2_out;

  and and_1 (and_1_out, G_0, P_1);
  and and_2 (and_2_out, C_0, P_1, P_0);
  or or_1 (C_2, G_1, and_1_out, and_2_out);
endmodule

module Carry_3 (
  input  C_0,
  input  P_0,
  input  P_1,
  input  P_2,
  input  G_0,
  input  G_1,
  input  G_2,
  output C_3
);

  wire and_1_out, and_2_out, and_3_out;

  and and_1 (and_1_out, C_0, P_0, P_1, P_2);
  and and_2 (and_2_out, P_1, P_2, G_0);
  and and_3 (and_3_out, P_2, G_1);
  or or_1 (C_3, and_1_out, and_2_out, and_3_out, G_2);
endmodule

module Full_CLA (
  input  A_0,
  input  A_1,
  input  Cin,
  input  A_2,
  input  B_0,
  input  B_1,
  input  B_2,
  output S_0,
  output S_1,
  output S_2,
  output C3
);

  wire C1_c_1, C2_c_2, G_0, G_1, G_2, P_0, P_1, P_2;

  Carry_1 C1 (.G_0(G_0), .C_0(Cin), .P_0(P_0), .C_1(C1_c_1));
  Carry_2 C2 (.G_1(G_1), .G_0(G_0), .C_0(Cin), .P_1(P_1), .P_0(P_0), .C_2(C2_c_2));
  Carry_3 u_C3 (.C_0(Cin), .P_0(P_0), .P_1(P_1), .P_2(P_2), .G_0(G_0), .G_1(G_1), .G_2(G_2), .C_3(C3));
  Carry_Look_Ahead CLA (.A(A_0), .B(B_0), .Cin(Cin), .Sum(S_0), .P(P_0), .G(G_0));
  Carry_Look_Ahead CLA_2 (.A(A_1), .B(B_1), .Cin(C1_c_1), .Sum(S_1), .P(P_1), .G(G_1));
  Carry_Look_Ahead CLA_3 (.A(A_2), .B(B_2), .Cin(C2_c_2), .Sum(S_2), .P(P_2), .G(G_2));
endmodule

module AND (
  input  A_0,
  input  B_0,
  input  A_1,
  input  B_1,
  input  A_2,
  input  B_2,
  output C_0,
  output C_1,
  output C_2
);

  and and_1 (C_0, A_0, B_0);
  and and_2 (C_1, A_1, B_1);
  and and_3 (C_2, A_2, B_2);
endmodule

module OR (
  input  A_0,
  input  B_0,
  input  A_1,
  input  B_1,
  input  A_2,
  input  B_2,
  output C_0,
  output C_1,
  output C_2
);

  or or_1 (C_0, A_0, B_0);
  or or_2 (C_1, A_1, B_1);
  or or_3 (C_2, A_2, B_2);
endmodule

module NOT (
  input  A_0,
  input  A_1,
  input  A_2,
  output C_0,
  output C_1,
  output C_2
);

  not not_1 (C_0, A_0);
  not not_2 (C_1, A_1);
  not not_3 (C_2, A_2);
endmodule

module ALU (
  input  [2:0] A_2__A_1__A_0,
  input  [2:0] B_2__B_1__B_0,
  input  Cin,
  input  [2:0] in_4,
  input  [2:0] in_5,
  output out_6
);

  wire A_0, A_1, B_0, B_1, B_2;
  wire [2:0] AND_c_0, Full_CLA_s_0, OR_c_0;

  NOT NOT (.A_0(A_0), .A_1(A_1), .A_2(A_1));  // open: C_0, C_1, C_2
  Full_CLA Full_CLA (
    .A_0(A_0), .A_1(A_1), .A_2(A_1), .B_0(B_0), .B_1(B_1), .B_2(B_2), .Cin(Cin), .S_0(Full_CLA_s_0[0]),
    .S_1(Full_CLA_s_0[1]), .S_2(Full_CLA_s_0[2]), .C3(out_6));
  AND AND (
    .A_0(A_0), .B_0(B_0), .A_1(A_1), .B_1(B_1), .A_2(A_1), .B_2(B_2), .C_0(AND_c_0[0]), .C_1(AND_c_0[1]),
    .C_2(AND_c_0[2]));
  OR OR (
    .A_0(A_0), .B_0(B_0), .A_1(A_1), .B_1(B_1), .A_2(A_1), .B_2(B_2), .C_0(OR_c_0[0]), .C_1(OR_c_0[1]),
    .C_2(OR_c_0[2]));
  Multiplexer #(.select(3), .width(3)) multiplexer_1 (
    .in0(AND_c_0), .in1(OR_c_0), .in3(Full_CLA_s_0), .out(in_5), .sel(in_4));  // open: in2, in4, in5, in6, in7, en

  // Other names for the same wires on the sheet: A_2 = A_1; S_2__S_1__S_0[2:0] = in_4
endmodule
