// Logisim project 3.1.circ as structural Verilog: 1 circuit, main circuit main
module main (
  input  in_1,
  output out_2
);

  wire and_1_out, and_2_out, and_3_out, clock_1_out, d_ff_1_q, d_ff_2_q, d_ff_2_qn, d_ff_3_qn, not_1_out;

  Clock clock_1 (.out(clock_1_out));
  not not_1 (not_1_out, in_1);
  D_Flip_Flop d_ff_1 (.clk(clock_1_out), .D(in_1), .Q(d_ff_1_q));  // open: Qn, preset, en, reset
  and and_1 (and_1_out, d_ff_2_qn, not_1_out);
  and and_2 (and_2_out, d_ff_3_qn, not_1_out);
  or or_1 (out_2, and_1_out, and_2_out, and_3_out);
  D_Flip_Flop d_ff_2 (.clk(clock_1_out), .D(d_ff_1_q), .Q(d_ff_2_q), .Qn(d_ff_2_qn));  // open: preset, en, reset
  and and_3 (and_3_out, d_ff_2_qn, d_ff_3_qn);
  D_Flip_Flop d_ff_3 (.clk(clock_1_out), .D(d_ff_2_q), .Qn(d_ff_3_qn));  // open: Q, preset, en, reset
endmodule
