// Logisim project 3.2.circ as structural Verilog: 1 circuit, main circuit main
module main (
  input  Nickel,
  input  Dime,
  output Give_Merchandise,
  output Give_Change
);

  wire and_1_out, and_2_out, and_3_out, and_4_out, and_5_out, and_6_out, and_7_out, and_8_out, and_9_out,
       and_10_out, and_11_out, and_12_out, and_13_out, and_14_out, BuyAnotherItem_out, d_ff_1_q, d_ff_2_q,
       d_ff_3_q, d_ff_4_q, d_ff_5_q, d_ff_6_q, d_ff_7_q, d_ff_8_q, d_ff_9_q, InsertCoin_out;

  Clock InsertCoin (.out(InsertCoin_out));
  Button BuyAnotherItem (.out(BuyAnotherItem_out));
  and and_1 (and_1_out, InsertCoin_out, Nickel);
  and and_2 (and_2_out, InsertCoin_out, Dime);
  D_Flip_Flop d_ff_1 (.clk(and_1_out), .D(Nickel), .Q(d_ff_1_q), .reset(BuyAnotherItem_out));  // open: Qn, preset
  D_Flip_Flop d_ff_2 (.clk(and_2_out), .D(Dime), .Q(d_ff_2_q), .reset(BuyAnotherItem_out));  // open: Qn, preset
  and and_3 (and_3_out, InsertCoin_out, Nickel);
  and and_4 (and_4_out, InsertCoin_out, Dime);
  D_Flip_Flop d_ff_3 (.clk(and_3_out), .D(d_ff_1_q), .Q(d_ff_3_q), .reset(BuyAnotherItem_out));  // open: Qn, preset
  D_Flip_Flop d_ff_4 (.clk(and_4_out), .D(d_ff_2_q), .Q(d_ff_4_q), .reset(BuyAnotherItem_out));  // open: Qn, preset
  and and_5 (and_5_out, InsertCoin_out, Nickel);
  D_Flip_Flop d_ff_5 (.clk(and_5_out), .D(d_ff_3_q), .Q(d_ff_5_q), .reset(BuyAnotherItem_out));  // open: Qn, preset
  and and_6 (and_6_out, InsertCoin_out, Dime);
  and and_7 (and_7_out, InsertCoin_out, Nickel);
  D_Flip_Flop d_ff_6 (.clk(and_6_out), .D(d_ff_4_q), .Q(d_ff_6_q), .reset(BuyAnotherItem_out));  // open: Qn, preset
  D_Flip_Flop d_ff_7 (.clk(and_7_out), .D(d_ff_5_q), .Q(d_ff_7_q), .reset(BuyAnotherItem_out));  // open: Qn, preset
  and and_8 (and_8_out, d_ff_5_q, d_ff_4_q);
  and and_9 (and_9_out, d_ff_3_q, d_ff_4_q);
  and and_10 (and_10_out, InsertCoin_out, Nickel);
  D_Flip_Flop d_ff_8 (.clk(and_10_out), .D(d_ff_7_q), .Q(d_ff_8_q), .reset(BuyAnotherItem_out));  // open: Qn, preset
  and and_11 (and_11_out, InsertCoin_out, Nickel);
  D_Flip_Flop d_ff_9 (.clk(and_11_out), .D(d_ff_8_q), .Q(d_ff_9_q), .reset(BuyAnotherItem_out));  // open: Qn, preset
  and and_12 (and_12_out, d_ff_8_q, d_ff_2_q);
  and and_13 (and_13_out, d_ff_7_q, d_ff_2_q);
  and and_14 (and_14_out, d_ff_6_q, d_ff_1_q);
  or or_1 (Give_Merchandise, d_ff_9_q, and_9_out, and_13_out, and_8_out, d_ff_6_q);
  or or_2 (Give_Change, and_12_out, and_8_out, and_14_out);

  // Notes on the sheet:
  //   Case 4: 3/2
  //   Case 5: 2/2
  //   Case 7: 0/3
  //   Case 1: 6/0
  //   Case 2: 5/1
  //   Case 6: 1/3
  //   Case 3: 4/1 & 5/1
endmodule
