// Logisim project LAB4.circ as structural Verilog
module implementation (
  input  [15:0] Instruction_In,
  input  ClkIn,
  input  [4:0] in_3,
  output [4:0] Instruction_Address_Out,
  output [3:0] Reg0_Out,
  output [3:0] Reg1_Out,
  output [3:0] Reg2_Out,
  output [3:0] Reg3_Out,
  output [3:0] Reg4_Out,
  output [3:0] Reg5_Out,
  output [3:0] Reg6_Out,
  output [3:0] Reg7_Out,
  output [3:0] Reg8_Out,
  output [3:0] Reg9_Out,
  output [3:0] Reg10_Out,
  output [3:0] Reg11_Out,
  output [3:0] Reg12_Out,
  output [3:0] Reg13_Out,
  output [3:0] Reg14_Out,
  output [3:0] Reg15_Out,
  output [3:0] WriteIn_Value
);

  wire and_1_out, and_4_out, not_1_out, not_2_out, not_3_out, not_4_out, not_5_out, not_6_out, not_7_out,
       not_9_out, Reset, ValidInput;
  wire [3:0] A_Value, ADDI_out_3, ADDR_out_3, ANDI_out_3, ANDR_out_3, B_Value, negator_1_out, NOT_8_out,
       ORI_out_3, ORR_out_3, SUBR_out_3, XORI_out_3, XORR_out_3;

  not not_1 (not_1_out, Instruction_In[15]);
  not not_2 (not_2_out, Instruction_In[15]);
  not not_3 (not_3_out, Instruction_In[14]);
  not not_4 (not_4_out, Instruction_In[13]);
  and and_1 (and_1_out, not_1_out, not_3_out, not_4_out);
  and and_2 (Reset, and_1_out, Instruction_In[12]);
  not not_5 (not_5_out, Instruction_In[14]);
  not not_6 (not_6_out, Instruction_In[13]);
  and and_3 (ValidInput, not_2_out, not_7_out, not_6_out);
  not not_7 (not_7_out, Instruction_In[12]);
  ADD ANDI (.Reg_A(A_Value), .Reg_B_Imm_e0292cfe(Instruction_In[3:0]), .out_3(ANDI_out_3));
  ADD ANDR (.Reg_A(A_Value), .Reg_B_Imm_e0292cfe(B_Value), .out_3(ANDR_out_3));
  OR ORI (.Reg_A(A_Value), .Reg_B_Imm_e0292cfe(Instruction_In[3:0]), .out_3(ORI_out_3));
  OR ORR (.Reg_A(A_Value), .Reg_B_Imm_e0292cfe(B_Value), .out_3(ORR_out_3));
  XOR XORI (.Reg_A(A_Value), .Reg_B_Imm_e0292cfe(Instruction_In[3:0]), .out_3(XORI_out_3));
  XOR XORR (.Reg_A(A_Value), .Reg_B_Imm_e0292cfe(B_Value), .out_3(XORR_out_3));
  Negator #(.width(4)) negator_1 (.in(A_Value), .out(negator_1_out));
  assign NOT_8_out = ~A_Value;  // NOT_Gate NOT_8, 4 bits wide
  ADD ADDI (.Reg_A(A_Value), .Reg_B_Imm_e0292cfe(Instruction_In[3:0]), .out_3(ADDI_out_3));
  ADD ADDR (.Reg_A(A_Value), .Reg_B_Imm_e0292cfe(B_Value), .out_3(ADDR_out_3));
  SUB SUBI (.Reg_A(A_Value), .Reg_B_Imm_e0292cfe(Instruction_In[3:0]), .out_3(ADDR_out_3));
  SUB SUBR (.Reg_A(A_Value), .Reg_B_Imm_e0292cfe(B_Value), .out_3(SUBR_out_3));
  RegFile regfile_1 (
    .A_Sel_In(Instruction_In[7:4]), .B_Sel_In(Instruction_In[3:0]), .C_Sel_In(Instruction_In[11:8]),
    .Data_In(WriteIn_Value), .Reg_Write_In(1'b1), .clk_in(ClkIn), .A_Out(A_Value), .B_Out(B_Value),
    .Reg0_Out(Reg0_Out), .Reg1_Out(Reg1_Out), .Reg2_Out(Reg2_Out), .Reg3_Out(Reg3_Out), .Reg4_Out(Reg4_Out),
    .Reg5_Out(Reg5_Out), .Reg6_Out(Reg6_Out), .Reg7_Out(Reg7_Out), .Reg8_Out(Reg8_Out), .Reg9_Out(Reg9_Out),
    .Reg10_Out(Reg10_Out), .Reg11_Out(Reg11_Out), .Reg12_Out(Reg12_Out), .Reg13_Out(Reg13_Out),
    .Reg14_Out(Reg14_Out), .Reg15_Out(Reg15_Out));
  Multiplexer #(.select(4), .width(4)) multiplexer_1 (
    .in2(A_Value), .in3(Instruction_In[3:0]), .in4(ANDI_out_3), .in5(ANDR_out_3), .in6(ORI_out_3),
    .in7(ORR_out_3), .in8(XORI_out_3), .in9(XORR_out_3), .in10(negator_1_out), .in11(NOT_8_out),
    .in12(ADDI_out_3), .in13(ADDR_out_3), .in14(ADDR_out_3), .in15(SUBR_out_3), .out(WriteIn_Value),
    .sel(Instruction_In[15:12]));  // open: in0, in1, en
  and and_4 (and_4_out, ClkIn, not_9_out);
  not not_9 (not_9_out, ValidInput);
  Counter #(.max('h1f), .width(5)) counter_1 (
    .load(Reset), .D(in_3), .Q(Instruction_Address_Out), .clk(and_4_out));  // open: count, carry, up, clr

  // Other names for the same wires on the sheet: Clk = ClkIn; Clock = ClkIn; Instruction[15:0] = Instruction_In;
  //   Instruction_Address[4:0] = Instruction_Address_Out; Reg0[3:0] = Reg0_Out; Reg1[3:0] = Reg1_Out;
  //   Reg2[3:0] = Reg2_Out; Reg3[3:0] = Reg3_Out; Reg4[3:0] = Reg4_Out; Reg5[3:0] = Reg5_Out; Reg6[3:0] = Reg6_Out;
  //   Reg7[3:0] = Reg7_Out; Reg8[3:0] = Reg8_Out; Reg9[3:0] = Reg9_Out; Reg10[3:0] = Reg10_Out;
  //   Reg11[3:0] = Reg11_Out; Reg12[3:0] = Reg12_Out; Reg13[3:0] = Reg13_Out; Reg14[3:0] = Reg14_Out;
  //   Reg15[3:0] = Reg15_Out

  // Notes on the sheet:
  //   Bits 0-3 is B and IMM
  //   Bits 4-7 is A
  //   Bits 8-11 is C
  //   BIts 12-15 is Opcode
  //   For IG demonstrate:
  //   ADDI, MOVE, ANDI, SUBR
  //   CPU needs to have a PC, Instruction Counter, and Register File 
  //   Represents a counter of how many instructions have been executed
endmodule

module RegFile (
  input  [3:0] A_Sel_In,
  input  [3:0] B_Sel_In,
  input  [3:0] C_Sel_In,
  input  [3:0] Data_In,
  input  Reg_Write_In,
  input  clk_in,
  output [3:0] A_Out,
  output [3:0] B_Out,
  output [3:0] Reg0_Out,
  output [3:0] Reg1_Out,
  output [3:0] Reg2_Out,
  output [3:0] Reg3_Out,
  output [3:0] Reg4_Out,
  output [3:0] Reg5_Out,
  output [3:0] Reg6_Out,
  output [3:0] Reg7_Out,
  output [3:0] Reg8_Out,
  output [3:0] Reg9_Out,
  output [3:0] Reg10_Out,
  output [3:0] Reg11_Out,
  output [3:0] Reg12_Out,
  output [3:0] Reg13_Out,
  output [3:0] Reg14_Out,
  output [3:0] Reg15_Out
);

  wire Reg_Write0, Reg_Write1, Reg_Write2, Reg_Write3, Reg_Write4, Reg_Write5, Reg_Write6, Reg_Write7,
       Reg_Write8, Reg_Write9, Reg_Write10, Reg_Write11, Reg_Write12, Reg_Write13, Reg_Write14, Reg_Write15;

  Demultiplexer #(.enable("false"), .select(4)) demultiplexer_1 (
    .out0(Reg_Write0), .out1(Reg_Write1), .out2(Reg_Write2), .out3(Reg_Write3), .out4(Reg_Write4),
    .out5(Reg_Write5), .out6(Reg_Write6), .out7(Reg_Write7), .out8(Reg_Write8), .out9(Reg_Write9),
    .out10(Reg_Write10), .out11(Reg_Write11), .out12(Reg_Write12), .out13(Reg_Write13), .out14(Reg_Write14),
    .out15(Reg_Write15), .in(Reg_Write_In), .sel(C_Sel_In));
  Register #(.width(4)) register_1 (.D(Data_In), .en(Reg_Write0), .clk(clk_in), .Q(Reg0_Out));  // open: clr
  Register #(.width(4)) register_2 (.D(Data_In), .en(Reg_Write4), .clk(clk_in), .Q(Reg4_Out));  // open: clr
  Register #(.width(4)) register_3 (.D(Data_In), .en(Reg_Write8), .clk(clk_in), .Q(Reg8_Out));  // open: clr
  Register #(.width(4)) register_4 (.D(Data_In), .en(Reg_Write12), .clk(clk_in), .Q(Reg12_Out));  // open: clr
  Register #(.width(4)) register_5 (.D(Data_In), .en(Reg_Write1), .clk(clk_in), .Q(Reg1_Out));  // open: clr
  Register #(.width(4)) register_6 (.D(Data_In), .en(Reg_Write5), .clk(clk_in), .Q(Reg5_Out));  // open: clr
  Register #(.width(4)) register_7 (.D(Data_In), .en(Reg_Write9), .clk(clk_in), .Q(Reg9_Out));  // open: clr
  Register #(.width(4)) register_8 (.D(Data_In), .en(Reg_Write13), .clk(clk_in), .Q(Reg13_Out));  // open: clr
  Register #(.width(4)) register_9 (.D(Data_In), .en(Reg_Write2), .clk(clk_in), .Q(Reg2_Out));  // open: clr
  Register #(.width(4)) register_10 (.D(Data_In), .en(Reg_Write6), .clk(clk_in), .Q(Reg6_Out));  // open: clr
  Register #(.width(4)) register_11 (.D(Data_In), .en(Reg_Write10), .clk(clk_in), .Q(Reg10_Out));  // open: clr
  Register #(.width(4)) register_12 (.D(Data_In), .en(Reg_Write14), .clk(clk_in), .Q(Reg14_Out));  // open: clr
  Register #(.width(4)) register_13 (.D(Data_In), .en(Reg_Write3), .clk(clk_in), .Q(Reg3_Out));  // open: clr
  Register #(.width(4)) register_14 (.D(Data_In), .en(Reg_Write7), .clk(clk_in), .Q(Reg7_Out));  // open: clr
  Register #(.width(4)) register_15 (.D(Data_In), .en(Reg_Write11), .clk(clk_in), .Q(Reg11_Out));  // open: clr
  Register #(.width(4)) register_16 (.D(Data_In), .en(Reg_Write15), .clk(clk_in), .Q(Reg15_Out));  // open: clr
  Multiplexer #(.enable("false"), .select(4), .width(4)) multiplexer_1 (
    .in0(Reg0_Out), .in1(Reg1_Out), .in2(Reg2_Out), .in3(Reg3_Out), .in4(Reg4_Out), .in5(Reg5_Out),
    .in6(Reg6_Out), .in7(Reg7_Out), .in8(Reg8_Out), .in9(Reg9_Out), .in10(Reg10_Out), .in11(Reg11_Out),
    .in12(Reg12_Out), .in13(Reg13_Out), .in14(Reg14_Out), .in15(Reg15_Out), .out(A_Out), .sel(A_Sel_In));
  Multiplexer #(.enable("false"), .select(4), .width(4)) multiplexer_2 (
    .in0(Reg0_Out), .in1(Reg1_Out), .in2(Reg2_Out), .in3(Reg3_Out), .in4(Reg4_Out), .in5(Reg5_Out),
    .in6(Reg6_Out), .in7(Reg7_Out), .in8(Reg8_Out), .in9(Reg9_Out), .in10(Reg10_Out), .in11(Reg11_Out),
    .in12(Reg12_Out), .in13(Reg13_Out), .in14(Reg14_Out), .in15(Reg15_Out), .out(B_Out), .sel(B_Sel_In));

  // Other names for the same wires on the sheet: A[3:0] = A_Out; A_Sel[3:0] = A_Sel_In; B[3:0] = B_Out;
  //   B_Sel[3:0] = B_Sel_In; C_Sel[3:0] = C_Sel_In; clk = clk_in; Data[3:0] = Data_In; Reg0[3:0] = Reg0_Out;
  //   Reg1[3:0] = Reg1_Out; Reg2[3:0] = Reg2_Out; Reg3[3:0] = Reg3_Out; Reg4[3:0] = Reg4_Out; Reg5[3:0] = Reg5_Out;
  //   Reg6[3:0] = Reg6_Out; Reg7[3:0] = Reg7_Out; Reg8[3:0] = Reg8_Out; Reg9[3:0] = Reg9_Out; Reg10[3:0] = Reg10_Out;
  //   Reg11[3:0] = Reg11_Out; Reg12[3:0] = Reg12_Out; Reg13[3:0] = Reg13_Out; Reg14[3:0] = Reg14_Out;
  //   Reg15[3:0] = Reg15_Out; Reg_Write = Reg_Write_In
endmodule

module AND (
  input  [3:0] Reg_A,
  input  [3:0] Reg_B_Imm_e0292cfe,
  output [3:0] out_3
);

  assign out_3 = Reg_A & Reg_B_Imm_e0292cfe;  // AND_Gate and_1, 4 bits wide
endmodule

module OR (
  input  [3:0] Reg_A,
  input  [3:0] Reg_B_Imm_e0292cfe,
  output [3:0] out_3
);

  assign out_3 = Reg_A | Reg_B_Imm_e0292cfe;  // OR_Gate or_1, 4 bits wide
endmodule

module XOR (
  input  [3:0] Reg_A,
  input  [3:0] Reg_B_Imm_e0292cfe,
  output [3:0] out_3
);

  assign out_3 = Reg_A ^ Reg_B_Imm_e0292cfe;  // XOR_Gate xor_1, 4 bits wide
endmodule

module ADD (
  input  [3:0] Reg_A,
  input  [3:0] Reg_B_Imm_e0292cfe,
  output [3:0] out_3
);

  Adder #(.width(4)) adder_1 (.a(Reg_A), .b(Reg_B_Imm_e0292cfe), .out(out_3));  // open: cin, cout
endmodule

module SUB (
  input  [3:0] Reg_A,
  input  [3:0] Reg_B_Imm_e0292cfe,
  output [3:0] out_3
);

  Subtractor #(.width(4)) subtractor_1 (.a(Reg_A), .b(Reg_B_Imm_e0292cfe), .out(out_3));  // open: bin, bout
endmodule

module ALU (
  input  [3:0] Reg_A,
  input  [3:0] Reg_B,
  input  [3:0] Imm,
  input  [3:0] OpCode,
  output [3:0] Output
);

  wire [3:0] ADDI_out_3, ADDR_out_3, ANDI_out_3, ANDR_out_3, negator_1_out, NOT_out, ORI_out_3, ORR_out_3,
       SUBR_out_3, XORI_out_3, XORR_out_3;

  ADD ANDI (.Reg_A(Reg_A), .Reg_B_Imm_e0292cfe(Imm), .out_3(ANDI_out_3));
  ADD ANDR (.Reg_A(Reg_A), .Reg_B_Imm_e0292cfe(Reg_B), .out_3(ANDR_out_3));
  OR ORI (.Reg_A(Reg_A), .Reg_B_Imm_e0292cfe(Imm), .out_3(ORI_out_3));
  OR ORR (.Reg_A(Reg_A), .Reg_B_Imm_e0292cfe(Reg_B), .out_3(ORR_out_3));
  XOR XORI (.Reg_A(Reg_A), .Reg_B_Imm_e0292cfe(Imm), .out_3(XORI_out_3));
  XOR XORR (.Reg_A(Reg_A), .Reg_B_Imm_e0292cfe(Reg_B), .out_3(XORR_out_3));
  Negator #(.width(4)) negator_1 (.in(Reg_A), .out(negator_1_out));
  assign NOT_out = ~Reg_A;  // NOT_Gate NOT, 4 bits wide
  ADD ADDI (.Reg_A(Reg_A), .Reg_B_Imm_e0292cfe(Imm), .out_3(ADDI_out_3));
  ADD ADDR (.Reg_A(Reg_A), .Reg_B_Imm_e0292cfe(Reg_B), .out_3(ADDR_out_3));
  SUB SUBI (.Reg_A(Reg_A), .Reg_B_Imm_e0292cfe(Imm), .out_3(ADDR_out_3));
  SUB SUBR (.Reg_A(Reg_A), .Reg_B_Imm_e0292cfe(Reg_B), .out_3(SUBR_out_3));
  Multiplexer #(.select(4), .width(4)) multiplexer_1 (
    .in2(Reg_A), .in3(Imm), .in4(ANDI_out_3), .in5(ANDR_out_3), .in6(ORI_out_3), .in7(ORR_out_3),
    .in8(XORI_out_3), .in9(XORR_out_3), .in10(negator_1_out), .in11(NOT_out), .in12(ADDI_out_3),
    .in13(ADDR_out_3), .in14(ADDR_out_3), .in15(SUBR_out_3), .out(Output), .sel(OpCode));  // open: in0, in1, en
endmodule
